# Fritzing sketch Transmitter (saved by Fritzing 0.9.3b)
breadboards: 1

parts:
  Part1 = Arduino Nano (Rev3.0)
  Part2 = Thumb Joystick [part_number="Joystick 1 (Esquerda)"]
  Part4 = NRF24L01+ Breakout Board
  Part5 = Thumb Joystick [part_number="Joystick 2 (Direita)"]

nets:
  GND: Part1.GND, Part2.GND, Part4.GND, Part5.GND
  N1: Part1.D7, Part4.CE
  N2: Part1.D8, Part4.CS
  N3: Part1.D11/MOSI, Part4.MOSI
  N4: Part1.D12/MISO, Part4.MISO
  VCC: Part1.5V, Part2.VCC, Part5.VCC
  N5: Part1.A3, Part5.VERT
  N6: Part1.A2, Part5.HORZ
  N7: Part1.A1, Part2.VERT
  N8: Part1.A0, Part2.HORZ
  3V3: Part1.3V3, Part4.VCC
  N9: Part1.D13/SCK, Part4.SCK
